# Fritzing sketch RotaryEncoder (saved by Fritzing 0.7.12b)
breadboards: 1

parts:
  C1 = Ceramic Capacitor [capacitance=100nF package="100 mil [THT, multilayer]"]
  C2 = Ceramic Capacitor [capacitance=100nF package="100 mil [THT, multilayer]"]
  ENCODER1 = Rotary Encoder with Knob
  Raspberry_Pi1 = Raspberry Pi (Model B)

nets:
  GND: C1.0, C1.1, C2.0, C2.1, ENCODER1.no_name_yet#1, ENCODER1.no_name_yet#3, Raspberry_Pi1.SDA, Raspberry_Pi1.SCL, Raspberry_Pi1.GND
  N1: ENCODER1.no_name_yet#2, Raspberry_Pi1.3V3

custom parts:
  Rotary Encoder with Knob: Rotary Encoder with 1/4" Shaft and Knob
  Raspberry Pi (Model B): Raspberry Pi Single-board Computer, Model B
